# Fritzing sketch Kitchen Light Bar 4x3 rev 7 (saved by Fritzing 0.9.3b)
circuit board: 10.16cm x 7.62cm
breadboards: 1

parts:
  Part2 = Arduino Nano (Rev3.0)
  Q1 = Basic FET N-Channel [package="TO220 [THT]"]
  S1 = Toggle Switch [package=THT]
  Q3 = Basic FET N-Channel [package="TO220 [THT]"]
  Q2 = Basic FET N-Channel [package="TO220 [THT]"]
  Part3 = HC-SR501 Body Sensor Module
  JP1 = Header 4 [package=jst-4-pth]
  Q4 = Basic FET N-Channel [package="TO220 [THT]"]
  JP2 = Header 2 [package=jst-2-pth]
  R1 = Resistor [tolerance=±5% resistance=220 package=THT]
  JP3 = Header 2 [package=screwterminal-3.5mm-2_lock]
  LED2 = LED - 5mm [color="Red (633nm)" package="5 mm [THT]"]

nets:
  GND: Part2.GND, Q1.source, Q3.source, Q2.source, Part3.GND, Q4.source, JP3.1, LED2.cathode
  N1: Part2.D3, Q3.gate
  N2: Part2.D5, Q2.gate
  N3: Part2.D6, Q1.gate
  N4: Part2.D9, Q4.gate
  N5: Part2.VIN, S1.L1, JP1.1, JP2.1
  5V: Part2.5V, Part3.VCC, R1.Pin_1
  N6: Part2.A6, Part3.OUT
  N7: Q1.drain, JP1.2
  N8: S1.COM, JP3.2
  N9: Q3.drain, JP1.4
  N10: Q2.drain, JP1.3
  N11: Q4.drain, JP2.2
  N12: R1.Pin_0, LED2.anode

notes:
  To 12V power supply

custom parts:
  HC-SR501 Body Sensor Module: Pyroelectric Infrared PIR Motion Sensor Detector Module
